# Fritzing sketch Fritzing Layout (saved by Fritzing 0.9.3b)
breadboards: 1

parts:
  STM32 = STM32 Nucleo boards
  Part1 = DB25M

nets:
  N1: STM32.PC6, Part1.pin19
  N2: STM32.PC5, Part1.pin17
  GND: STM32.GND, Part1.pin7, Part1.pin9, Part1.pin14, Part1.pin16, Part1.pin18, Part1.pin24
  N3: STM32.PB2, Part1.pin22
  N4: STM32.PB1, Part1.pin21
  N5: STM32.PC4, Part1.pin15
  N6: STM32.PB8, Part1.pin20
  N7: STM32.PB6, Part1.pin12
  N8: STM32.PC7, Part1.pin5
  N9: STM32.PB4, Part1.pin23
  N10: STM32.PB5, Part1.pin11
  N11: STM32.PB3, Part1.pin10
  N12: STM32.PA0, Part1.pin4
  N13: STM32.PB0, Part1.pin8
  N14: STM32.PC1, Part1.pin6
  N15: STM32.PC0, Part1.pin2
  N16: STM32.PB7, Part1.pin13
  N17: STM32.PC2, Part1.pin1
  N18: STM32.PC3, Part1.pin3
